// Logisim project alu.circ as structural Verilog: 2 circuits, main circuit alu
module alu (
  input  [31:0] A,
  input  [31:0] B,
  input  [3:0] ALUSel,
  output [31:0] Result
);

  wire comparator_2_eq, xor_2_out;
  wire [0:0] slt7;
  wire [31:0] add0, adder_2_out, and1, bit_flip_1_out_2, div8, mul10, mulh14, mulhu11, multiplexer_1_out,
       multiplexer_2_out, multiplexer_3_out, multiplier_2_cout, multiplier_2_out, negator_1_out,
       negator_2_out, or2, ref9, sll6, sra5, srl4, sub12, xor3;

  Negator #(.width(32)) negator_1 (.in(A), .out(negator_1_out));
  Negator #(.width(32)) negator_2 (.in(B), .out(negator_2_out));
  Adder #(.width(32)) adder_1 (.a(A), .b(B), .out(add0));  // open: cin, cout
  Subtractor #(.width(32)) subtractor_1 (.a(A), .b(B), .out(sub12));  // open: bin, bout
  assign and1 = A & B;  // AND_Gate and_1, 32 bits wide
  assign or2 = A | B;  // OR_Gate or_1, 32 bits wide
  assign xor3 = A ^ B;  // XOR_Gate xor_1, 32 bits wide
  Shifter #(.width(32), .shift("lr")) shifter_1 (.in(A), .\dist (B[4:0]), .out(srl4));
  Shifter #(.width(32), .shift("ar")) shifter_2 (.in(A), .\dist (B[4:0]), .out(sra5));
  Shifter #(.width(32)) shifter_3 (.in(A), .\dist (B[4:0]), .out(sll6));
  Comparator #(.width(32)) comparator_1 (.a(A), .b(B), .lt(slt7[0]));  // open: gt, eq
  Multiplier #(.width(32)) multiplier_1 (.a(A), .b(B), .out(mul10), .cout(mulhu11));  // open: cin
  Subtractor #(.width(32)) subtractor_2 (.a(A), .b(B), .out(sub12));  // open: bin, bout
  Multiplexer #(.width(32), .enable("false")) multiplexer_1 (
    .in0(A), .in1(negator_1_out), .out(multiplexer_1_out), .sel(A[31]));
  Multiplexer #(.width(32), .enable("false")) multiplexer_2 (
    .in0(B), .in1(negator_2_out), .out(multiplexer_2_out), .sel(B[31]));
  Divider #(.width(32)) divider_1 (.a(A), .b(B), .out(div8), .rem(ref9));  // open: upper
  Multiplier #(.width(32)) multiplier_2 (
    .a(multiplexer_1_out), .b(multiplexer_2_out), .out(multiplier_2_out), .cout(multiplier_2_cout));  // open: cin
  xor xor_2 (xor_2_out, A[31], B[31]);
  Comparator #(.width(32)) comparator_2 (.a({32{1'b0}}), .b(multiplier_2_out), .eq(comparator_2_eq));  // open: gt, lt
  bit_flip bit_flip_1 (.in_1(multiplier_2_cout), .out_2(bit_flip_1_out_2));
  Multiplexer #(.width(32), .enable("false")) multiplexer_3 (
    .in0(bit_flip_1_out_2), .in1(adder_2_out), .out(multiplexer_3_out), .sel(comparator_2_eq));
  Adder #(.width(32)) adder_2 (.a(bit_flip_1_out_2), .b(32'h1), .out(adder_2_out));  // open: cin, cout
  Multiplexer #(.select(4), .width(32), .enable("false")) multiplexer_4 (
    .in0(add0), .in1(and1), .in2(or2), .in3(xor3), .in4(srl4), .in5(sra5), .in6(sll6),
    .in7({{31{1'b0}}, slt7[0]}), .in8(div8), .in9(ref9), .in10(mul10), .in11(mulhu11), .in12(sub12),
    .in13(B), .in14(mulh14), .in15(A), .out(Result), .sel(ALUSel));
  Multiplexer #(.width(32), .enable("false")) multiplexer_5 (
    .in0(multiplier_2_cout), .in1(multiplexer_3_out), .out(mulh14), .sel(xor_2_out));

  // Other names for the same wires on the sheet: Asel15[31:0] = A; Bsel13[31:0] = B

  // Notes on the sheet:
  //   INPUTS to your circuit
  //   DON'T CHANGE THE LOCATIONS OF THE INPUTS AND OUTPUTS!
  //   OUTPUT from your circuit
endmodule

module bit_flip (
  input  [31:0] in_1,
  output [31:0] out_2
);

  assign out_2 = in_1 ^ {32{1'b1}};  // XOR_Gate xor_1, 32 bits wide
endmodule
