// Logisim project branch_comp.circ as structural Verilog: 1 circuit, main circuit branch_comp
module branch_comp (
  input  [31:0] rs1,
  input  [31:0] rs2,
  input  BrUn,
  output BrEq,
  output BrLt
);

  wire comparator_1_gt, Seq, Slt, Ueq, Ult;

  Comparator #(.width(32)) comparator_1 (.a(rs1), .b(rs2), .gt(comparator_1_gt), .eq(Seq), .lt(Slt));
  Comparator #(.width(32), .mode("unsigned")) comparator_2 (.a(rs1), .b(rs2), .eq(Ueq), .lt(Ult));  // open: gt
  Multiplexer #(.enable("false")) multiplexer_1 (.in0(Seq), .in1(Ueq), .out(BrEq), .sel(BrUn));
  Multiplexer #(.enable("false")) multiplexer_2 (.in0(Slt), .in1(Ult), .out(BrLt), .sel(BrUn));

  // Notes on the sheet:
  //   INPUTS to your circuit
  //   DON'T CHANGE THE LOCATIONS OF THE INPUTS AND OUTPUTS!
  //   OUTPUT from your circuit
endmodule
