// Logisim project control_logic.circ as structural Verilog: 2 circuits, main circuit control_logic
module control_logic (
  input  [31:0] inst,
  input  BrEq,
  input  BrLt,
  output PCSel,
  output RegWEn,
  output [2:0] ImmSel,
  output BrUn,
  output ASel,
  output BSel,
  output [3:0] ALUSel,
  output MemRW,
  output [1:0] WBSel
);

  wire and_1_out, B_Con, decoder_1_out0, multiplexer_3_out, not_1_out, not_2_out, not_3_out, not_4_out;
  wire [5:0] address_decoder_1_address;
  wire [15:2] rom_1_data;

  address_decoder address_decoder_1 (
    .opcode(inst[6:2]), .func3(inst[14:12]), .func7(inst[31:25]), .address(address_decoder_1_address));
  ROM #(.addrWidth(6), .dataWidth(16)) rom_1 (
    .addr(address_decoder_1_address),
    .data({rom_1_data[15:14], RegWEn, ImmSel, BrUn, ASel, BSel, ALUSel, rom_1_data[2], WBSel}));
  Multiplexer #(.enable("false")) multiplexer_1 (.in0(rom_1_data[14]), .in1(B_Con), .out(PCSel), .sel(rom_1_data[15]));
  not not_1 (not_1_out, BrEq);
  not not_2 (not_2_out, BrLt);
  not not_3 (not_3_out, BrEq);
  and and_1 (and_1_out, not_3_out, not_4_out);
  not not_4 (not_4_out, BrLt);
  Decoder decoder_1 (.out0(decoder_1_out0), .out1(MemRW), .sel(multiplexer_3_out), .en(rom_1_data[2]));
  Multiplexer #(.select(2), .enable("false")) multiplexer_2 (
    .in0(BrEq), .in1(not_1_out), .in2(BrLt), .in3(not_2_out), .out(B_Con), .sel({inst[14], inst[12]}));
  Multiplexer #(.enable("false")) multiplexer_3 (.in0(1'b1), .in1(and_1_out), .out(multiplexer_3_out), .sel(inst[12]));

  // Other names for the same wires on the sheet: Bran_sel[1:0] = {inst[14], inst[12]}

  // Notes on the sheet:
  //   INPUTS to your circuit
  //   contents of rom_1 (hex, n*v repeats v):
  //   3c01 3c51 3c61 3c31 3c71 3c59 3c39 3c19 3c21 3c29 3c11 3c09 2083 2083 2082 2081 20b1 20b9 2099 20a1
  //   20a9 2091 2089 3c41 484 47c 4*8980 8b80 8b80 2d81 2ce9 7180 6080 3c49
  //   DON'T CHANGE THE LOCATIONS OF THE INPUTS AND OUTPUTS!
  //   OUTPUT from your circuit
endmodule

module address_decoder (
  input  [4:0] opcode,
  input  [2:0] func3,
  input  [6:0] func7,
  output [5:0] address
);

  wire and_1_out, and_2_out, and_3_out, and_4_out, and_5_out, and_6_out, and_7_out, and_8_out, and_9_out,
       and_10_out, and_11_out, and_12_out, and_13_out, and_14_out, and_15_out, and_16_out, and_17_out,
       and_21_out, and_23_out, and_24_out, and_25_out, and_26_out, and_27_out, and_28_out, and_29_out,
       and_31_out, and_32_out, and_33_out, and_34_out, and_35_out, and_36_out, and_37_out, and_38_out,
       and_39_out, and_40_out, and_41_out, and_42_out, and_43_out, and_44_out, and_45_out, and_46_out,
       and_47_out, and_48_out, and_49_out, and_50_out, and_51_out, and_52_out, and_53_out, and_54_out,
       and_55_out, and_56_out, and_57_out, and_58_out, and_59_out, and_60_out, and_61_out, and_62_out,
       and_63_out, and_64_out, and_65_out, and_66_out, and_67_out, and_68_out, and_69_out, and_70_out,
       and_71_out, and_72_out, and_73_out, and_74_out, and_75_out, and_76_out, and_77_out, and_78_out,
       and_79_out, and_80_out, and_81_out, and_82_out, and_83_out, and_84_out, and_85_out, and_86_out,
       and_87_out, and_88_out, and_89_out, and_90_out, and_91_out, and_92_out, and_93_out, and_94_out,
       and_95_out, and_96_out, and_97_out, and_98_out, and_99_out, and_100_out, and_101_out, and_102_out,
       and_103_out, and_104_out, and_105_out, and_106_out, and_107_out, and_108_out, and_109_out,
       and_110_out, and_111_out, and_112_out, and_113_out, and_114_out, and_115_out, and_116_out,
       and_117_out, and_118_out, and_119_out, and_120_out, and_121_out, and_122_out, and_123_out,
       and_124_out, and_125_out, and_126_out, and_127_out, and_128_out, and_129_out, and_130_out,
       and_131_out, and_132_out, and_133_out, and_134_out, and_135_out, and_136_out, and_137_out, not_1_out,
       not_2_out, not_3_out, not_4_out, not_5_out, not_6_out, not_7_out, not_8_out, not_9_out, not_10_out,
       not_11_out, not_12_out, not_13_out, not_14_out, not_15_out, not_16_out, not_17_out, not_18_out,
       not_19_out, not_20_out, not_21_out, not_22_out, not_23_out, not_24_out, not_25_out, not_26_out,
       not_27_out, not_28_out, not_29_out, not_30_out, not_31_out, not_32_out, not_33_out, not_34_out,
       not_35_out, not_36_out, not_37_out, not_38_out, not_39_out, not_40_out, not_41_out, not_42_out,
       not_43_out, not_44_out, not_45_out, not_46_out, not_47_out, not_48_out, not_49_out, not_50_out,
       not_51_out, not_52_out, not_53_out, not_54_out, not_55_out, not_56_out, not_57_out, not_58_out,
       not_59_out, not_60_out, not_61_out, not_62_out, not_63_out, not_64_out, not_65_out, not_66_out,
       not_67_out, not_68_out, not_69_out, not_70_out, not_71_out;
  wire [0:0] I03_type, I13_type, R_type, S_type, SB_type;
  wire [5:0] I03_type_address, I13_type_address, jalr_type_address, multiplexer_5_out, multiplexer_6_out,
       multiplexer_7_out, multiplexer_8_out, multiplexer_9_out, multiplexer_10_out, multiplexer_11_out,
       multiplexer_12_out, multiplexer_13_out, multiplexer_14_out, multiplexer_15_out, multiplexer_16_out,
       multiplexer_17_out, multiplexer_18_out, multiplexer_19_out, multiplexer_20_out, multiplexer_21_out,
       multiplexer_22_out, multiplexer_23_out, multiplexer_24_out, multiplexer_25_out, multiplexer_26_out,
       multiplexer_27_out, multiplexer_28_out, multiplexer_29_out, multiplexer_30_out, multiplexer_31_out,
       multiplexer_32_out, multiplexer_33_out, multiplexer_34_out, multiplexer_35_out, multiplexer_36_out,
       or_1_out, or_2_out, or_3_out, or_4_out, or_5_out, or_6_out, or_7_out, or_9_out, or_10_out, or_12_out,
       or_13_out, or_14_out, or_15_out, or_16_out, or_17_out, or_18_out, or_19_out, or_20_out, or_22_out,
       or_24_out, or_25_out, or_26_out, or_27_out, or_28_out, or_29_out, or_31_out, or_32_out, or_33_out,
       or_35_out, R_type_address, S_type_address, SB_type_address, U1_type_address, U_type_address,
       Uj_type_address;

  not not_1 (not_1_out, opcode[1]);
  not not_2 (not_2_out, opcode[2]);
  not not_3 (not_3_out, opcode[0]);
  not not_4 (not_4_out, opcode[4]);
  not not_5 (not_5_out, opcode[2]);
  not not_6 (not_6_out, opcode[3]);
  not not_7 (not_7_out, opcode[4]);
  not not_8 (not_8_out, opcode[0]);
  and and_1 (and_1_out, not_8_out, opcode[2]);
  not not_9 (not_9_out, opcode[3]);
  not not_10 (not_10_out, opcode[4]);
  and and_2 (and_2_out, not_9_out, not_10_out);
  not not_11 (not_11_out, opcode[2]);
  and and_3 (and_3_out, not_11_out, opcode[3]);
  not not_12 (not_12_out, opcode[4]);
  and and_4 (and_4_out, not_13_out, not_14_out);
  not not_13 (not_13_out, opcode[0]);
  not not_14 (not_14_out, opcode[1]);
  not not_15 (not_15_out, opcode[2]);
  and and_5 (and_5_out, opcode[3], opcode[4]);
  and and_6 (and_6_out, opcode[0], not_16_out);
  not not_16 (not_16_out, opcode[1]);
  not not_17 (not_17_out, opcode[3]);
  not not_18 (not_18_out, opcode[4]);
  and and_7 (and_7_out, not_17_out, not_18_out);
  and and_8 (and_8_out, opcode[0], not_19_out);
  not not_19 (not_19_out, opcode[1]);
  not not_20 (not_20_out, opcode[4]);
  and and_9 (and_9_out, opcode[3], not_20_out);
  and and_10 (and_10_out, opcode[0], opcode[1]);
  not not_21 (not_21_out, opcode[2]);
  and and_11 (and_11_out, opcode[3], opcode[4]);
  and and_12 (and_12_out, opcode[0], not_1_out);
  and and_13 (and_13_out, not_2_out, and_14_out);
  and and_14 (and_14_out, opcode[3], opcode[4]);
  and and_15 (and_15_out, opcode[2], opcode[3]);
  and and_16 (and_16_out, and_15_out, not_4_out);
  and and_17 (and_17_out, not_5_out, not_6_out);
  and and_18 (I03_type[0], and_17_out, not_7_out);
  and and_19 (I13_type[0], and_1_out, and_2_out);
  and and_20 (S_type[0], and_3_out, not_12_out);
  and and_21 (and_21_out, and_4_out, not_15_out);
  and and_22 (SB_type[0], and_21_out, and_5_out);
  and and_23 (and_23_out, and_6_out, and_24_out);
  and and_24 (and_24_out, opcode[2], and_7_out);
  and and_25 (and_25_out, and_8_out, and_26_out);
  and and_26 (and_26_out, opcode[2], and_9_out);
  and and_27 (and_27_out, and_10_out, and_28_out);
  and and_28 (and_28_out, not_21_out, and_11_out);
  Multiplexer #(.width(6), .enable("false")) multiplexer_1 (
    .in0({6{1'b0}}), .in1(6'b100011), .out(jalr_type_address), .sel(and_29_out));
  and and_29 (and_29_out, and_12_out, and_13_out);
  assign or_1_out = R_type_address | S_type_address;  // OR_Gate or_1, 6 bits wide
  assign or_2_out = jalr_type_address | Uj_type_address;  // OR_Gate or_2, 6 bits wide
  assign or_3_out = I03_type_address | I13_type_address;  // OR_Gate or_3, 6 bits wide
  assign or_4_out = U_type_address | U1_type_address;  // OR_Gate or_4, 6 bits wide
  and and_30 (R_type[0], not_3_out, and_16_out);
  Multiplexer #(.width(6), .enable("false")) multiplexer_2 (
    .in0({6{1'b0}}), .in1(6'b100001), .out(U1_type_address), .sel(and_25_out));
  Multiplexer #(.width(6), .enable("false")) multiplexer_3 (
    .in0({6{1'b0}}), .in1(6'b100010), .out(Uj_type_address), .sel(and_27_out));
  assign or_5_out = or_1_out | or_2_out;  // OR_Gate or_5, 6 bits wide
  assign or_6_out = or_3_out | SB_type_address;  // OR_Gate or_6, 6 bits wide
  Multiplexer #(.width(6), .enable("false")) multiplexer_4 (
    .in0({6{1'b0}}), .in1(6'b100000), .out(U_type_address), .sel(and_23_out));
  assign or_7_out = or_5_out | or_6_out;  // OR_Gate or_7, 6 bits wide
  assign address = or_7_out | or_4_out;  // OR_Gate or_8, 6 bits wide
  not not_22 (not_22_out, func3[0]);
  not not_23 (not_23_out, func3[1]);
  not not_24 (not_24_out, func3[2]);
  not not_25 (not_25_out, func7[0]);
  not not_26 (not_26_out, func3[1]);
  not not_27 (not_27_out, func3[2]);
  not not_28 (not_28_out, func7[0]);
  not not_29 (not_29_out, func3[1]);
  not not_30 (not_30_out, func3[2]);
  not not_31 (not_31_out, func3[2]);
  not not_32 (not_32_out, func3[0]);
  not not_33 (not_33_out, func3[2]);
  not not_34 (not_34_out, func3[0]);
  not not_35 (not_35_out, func3[1]);
  not not_36 (not_36_out, func3[1]);
  not not_37 (not_37_out, func7[0]);
  not not_38 (not_38_out, func7[5]);
  not not_39 (not_39_out, func3[1]);
  not not_40 (not_40_out, func3[0]);
  not not_41 (not_41_out, func7[0]);
  not not_42 (not_42_out, func3[1]);
  not not_43 (not_43_out, func7[5]);
  not not_44 (not_44_out, func3[0]);
  and and_31 (and_31_out, R_type[0], ~func3[0]);  // AND_Gate
  not not_45 (not_45_out, func3[2]);
  not not_46 (not_46_out, func7[5]);
  and and_32 (and_32_out, not_25_out, func7[5]);
  and and_33 (and_33_out, R_type[0], func3[0]);
  and and_34 (and_34_out, not_27_out, not_28_out);
  and and_35 (and_35_out, R_type[0], func3[0]);
  and and_36 (and_36_out, not_30_out, func7[0]);
  and and_37 (and_37_out, R_type[0], func3[0]);
  and and_38 (and_38_out, R_type[0], not_32_out);
  and and_39 (and_39_out, R_type[0], not_34_out);
  and and_40 (and_40_out, R_type[0], func3[0]);
  and and_41 (and_41_out, not_37_out, not_38_out);
  and and_42 (and_42_out, R_type[0], func3[0]);
  and and_43 (and_43_out, R_type[0], not_40_out);
  and and_44 (and_44_out, R_type[0], func3[0]);
  and and_45 (and_45_out, func3[2], not_41_out);
  and and_46 (and_46_out, R_type[0], func3[0]);
  and and_47 (and_47_out, func7[0], not_43_out);
  and and_48 (and_48_out, R_type[0], func3[0]);
  and and_49 (and_49_out, func3[2], func7[0]);
  and and_50 (and_50_out, S_type[0], func3[0]);
  and and_51 (and_51_out, and_50_out, and_52_out);
  and and_52 (and_52_out, func3[1], func3[2]);
  and and_53 (and_53_out, S_type[0], not_44_out);
  and and_54 (and_54_out, and_31_out, ~func3[1]);  // AND_Gate
  and and_55 (and_55_out, R_type[0], not_22_out);
  and and_56 (and_56_out, and_55_out, not_23_out);
  and and_57 (and_57_out, and_33_out, not_26_out);
  and and_58 (and_58_out, and_57_out, and_34_out);
  and and_59 (and_59_out, and_35_out, not_29_out);
  and and_60 (and_60_out, and_59_out, and_36_out);
  and and_61 (and_61_out, and_37_out, func3[1]);
  and and_62 (and_62_out, and_61_out, not_31_out);
  and and_63 (and_63_out, and_38_out, func3[1]);
  and and_64 (and_64_out, and_63_out, not_33_out);
  and and_65 (and_65_out, and_39_out, not_35_out);
  and and_66 (and_66_out, and_65_out, func3[2]);
  and and_67 (and_67_out, and_40_out, not_36_out);
  and and_68 (and_68_out, and_67_out, func3[2]);
  and and_69 (and_69_out, and_42_out, not_39_out);
  and and_70 (and_70_out, and_69_out, func3[2]);
  and and_71 (and_71_out, and_43_out, func3[1]);
  and and_72 (and_72_out, and_71_out, func3[2]);
  and and_73 (and_73_out, and_44_out, func3[1]);
  and and_74 (and_74_out, and_73_out, and_45_out);
  and and_75 (and_75_out, and_46_out, not_42_out);
  and and_76 (and_76_out, and_75_out, func3[2]);
  and and_77 (and_77_out, and_48_out, func3[1]);
  and and_78 (and_78_out, and_77_out, and_49_out);
  Multiplexer #(.width(6), .enable("false")) multiplexer_5 (
    .in0({6{1'b0}}), .in1(6'b011001), .out(multiplexer_5_out), .sel(and_51_out));
  Multiplexer #(.width(6), .enable("false")) multiplexer_6 (
    .in0({6{1'b0}}), .in1(6'b011000), .out(multiplexer_6_out), .sel(and_79_out));
  and and_79 (and_79_out, and_53_out, func3[1]);
  and and_80 (and_80_out, and_54_out, not_45_out);
  and and_81 (and_81_out, and_80_out, and_82_out);
  and and_82 (and_82_out, func7[0], not_46_out);
  and and_83 (and_83_out, and_56_out, not_24_out);
  and and_84 (and_84_out, and_83_out, and_32_out);
  Multiplexer #(.width(6), .enable("false")) multiplexer_7 (
    .in0({6{1'b0}}), .in1(6'b000011), .out(multiplexer_7_out), .sel(and_58_out));
  Multiplexer #(.width(6), .enable("false")) multiplexer_8 (
    .in0({6{1'b0}}), .in1(6'b000100), .out(multiplexer_8_out), .sel(and_60_out));
  Multiplexer #(.width(6), .enable("false")) multiplexer_9 (
    .in0({6{1'b0}}), .in1(6'b000101), .out(multiplexer_9_out), .sel(and_62_out));
  Multiplexer #(.width(6), .enable("false")) multiplexer_10 (
    .in0({6{1'b0}}), .in1(6'b000110), .out(multiplexer_10_out), .sel(and_64_out));
  Multiplexer #(.width(6), .enable("false")) multiplexer_11 (
    .in0({6{1'b0}}), .in1(6'b000111), .out(multiplexer_11_out), .sel(and_66_out));
  Multiplexer #(.width(6), .enable("false")) multiplexer_12 (
    .in0({6{1'b0}}), .in1(6'b001000), .out(multiplexer_12_out), .sel(and_85_out));
  and and_85 (and_85_out, and_68_out, and_41_out);
  Multiplexer #(.width(6), .enable("false")) multiplexer_13 (
    .in0({6{1'b0}}), .in1(6'b001001), .out(multiplexer_13_out), .sel(and_86_out));
  and and_86 (and_86_out, and_70_out, func7[5]);
  Multiplexer #(.width(6), .enable("false")) multiplexer_14 (
    .in0({6{1'b0}}), .in1(6'b001010), .out(multiplexer_14_out), .sel(and_72_out));
  Multiplexer #(.width(6), .enable("false")) multiplexer_15 (
    .in0({6{1'b0}}), .in1(6'b001011), .out(multiplexer_15_out), .sel(and_74_out));
  Multiplexer #(.width(6), .enable("false")) multiplexer_16 (
    .in0({6{1'b0}}), .in1(6'b010111), .out(multiplexer_16_out), .sel(and_87_out));
  and and_87 (and_87_out, and_76_out, and_47_out);
  Multiplexer #(.width(6), .enable("false")) multiplexer_17 (
    .in0({6{1'b0}}), .in1(6'b100100), .out(multiplexer_17_out), .sel(and_78_out));
  Multiplexer #(.width(6), .enable("false")) multiplexer_18 (
    .in0({6{1'b0}}), .in1(6'b000010), .out(multiplexer_18_out), .sel(and_84_out));
  assign or_9_out = multiplexer_7_out | multiplexer_8_out;  // OR_Gate or_9, 6 bits wide
  assign or_10_out = multiplexer_13_out | multiplexer_14_out;  // OR_Gate or_10, 6 bits wide
  assign S_type_address = multiplexer_5_out | multiplexer_6_out;  // OR_Gate or_11, 6 bits wide
  Multiplexer #(.width(6), .enable("false")) multiplexer_19 (
    .in0({6{1'b0}}), .in1(6'b000001), .out(multiplexer_19_out), .sel(and_81_out));
  assign or_12_out = multiplexer_9_out | multiplexer_10_out;  // OR_Gate or_12, 6 bits wide
  assign or_13_out = or_12_out | or_14_out;  // OR_Gate or_13, 6 bits wide
  assign or_14_out = multiplexer_11_out | multiplexer_12_out;  // OR_Gate or_14, 6 bits wide
  assign or_15_out = or_10_out | multiplexer_15_out;  // OR_Gate or_15, 6 bits wide
  assign or_16_out = multiplexer_16_out | multiplexer_17_out;  // OR_Gate or_16, 6 bits wide
  assign or_17_out = multiplexer_19_out | multiplexer_18_out;  // OR_Gate or_17, 6 bits wide
  assign or_18_out = or_17_out | or_9_out;  // OR_Gate or_18, 6 bits wide
  assign or_19_out = or_13_out | or_20_out;  // OR_Gate or_19, 6 bits wide
  assign or_20_out = or_15_out | or_16_out;  // OR_Gate or_20, 6 bits wide
  assign R_type_address = or_18_out | or_19_out;  // OR_Gate or_21, 6 bits wide
  not not_47 (not_47_out, func3[0]);
  not not_48 (not_48_out, func3[1]);
  not not_49 (not_49_out, func3[1]);
  not not_50 (not_50_out, func3[0]);
  not not_51 (not_51_out, func3[1]);
  not not_52 (not_52_out, func3[2]);
  not not_53 (not_53_out, func3[1]);
  not not_54 (not_54_out, func3[2]);
  not not_55 (not_55_out, func3[0]);
  not not_56 (not_56_out, func3[2]);
  not not_57 (not_57_out, func3[0]);
  not not_58 (not_58_out, func3[1]);
  not not_59 (not_59_out, func3[1]);
  not not_60 (not_60_out, func7[5]);
  not not_61 (not_61_out, func3[1]);
  not not_62 (not_62_out, func3[0]);
  and and_88 (and_88_out, I03_type[0], not_47_out);
  and and_89 (and_89_out, I03_type[0], func3[0]);
  and and_90 (and_90_out, I03_type[0], func3[0]);
  and and_91 (and_91_out, I13_type[0], not_50_out);
  and and_92 (and_92_out, I13_type[0], func3[0]);
  and and_93 (and_93_out, and_92_out, not_53_out);
  and and_94 (and_94_out, I13_type[0], not_55_out);
  and and_95 (and_95_out, I13_type[0], not_57_out);
  and and_96 (and_96_out, I13_type[0], func3[0]);
  and and_97 (and_97_out, I13_type[0], func3[0]);
  and and_98 (and_98_out, I13_type[0], not_62_out);
  and and_99 (and_99_out, I13_type[0], func3[0]);
  Multiplexer #(.width(6), .enable("false")) multiplexer_20 (
    .in0({6{1'b0}}), .in1(6'b001100), .out(multiplexer_20_out), .sel(and_100_out));
  and and_100 (and_100_out, and_88_out, not_48_out);
  Multiplexer #(.width(6), .enable("false")) multiplexer_21 (
    .in0({6{1'b0}}), .in1(6'b001101), .out(multiplexer_21_out), .sel(and_101_out));
  and and_101 (and_101_out, and_89_out, not_49_out);
  Multiplexer #(.width(6), .enable("false")) multiplexer_22 (
    .in0({6{1'b0}}), .in1(6'b001110), .out(multiplexer_22_out), .sel(and_102_out));
  and and_102 (and_102_out, and_90_out, func3[1]);
  and and_103 (and_103_out, and_91_out, not_51_out);
  and and_104 (and_104_out, and_103_out, not_52_out);
  and and_105 (and_105_out, and_93_out, not_54_out);
  and and_106 (and_106_out, and_94_out, func3[1]);
  and and_107 (and_107_out, and_106_out, not_56_out);
  and and_108 (and_108_out, and_95_out, not_58_out);
  and and_109 (and_109_out, and_108_out, func3[2]);
  and and_110 (and_110_out, and_96_out, not_59_out);
  and and_111 (and_111_out, and_110_out, func3[2]);
  and and_112 (and_112_out, and_97_out, not_61_out);
  and and_113 (and_113_out, and_112_out, func3[2]);
  and and_114 (and_114_out, and_98_out, func3[1]);
  and and_115 (and_115_out, and_114_out, func3[2]);
  and and_116 (and_116_out, and_99_out, func3[1]);
  and and_117 (and_117_out, and_116_out, func3[2]);
  assign or_22_out = multiplexer_20_out | multiplexer_21_out;  // OR_Gate or_22, 6 bits wide
  Multiplexer #(.width(6), .enable("false")) multiplexer_23 (
    .in0({6{1'b0}}), .in1(6'b001111), .out(multiplexer_23_out), .sel(and_104_out));
  Multiplexer #(.width(6), .enable("false")) multiplexer_24 (
    .in0({6{1'b0}}), .in1(6'b010000), .out(multiplexer_24_out), .sel(and_105_out));
  Multiplexer #(.width(6), .enable("false")) multiplexer_25 (
    .in0({6{1'b0}}), .in1(6'b010001), .out(multiplexer_25_out), .sel(and_107_out));
  Multiplexer #(.width(6), .enable("false")) multiplexer_26 (
    .in0({6{1'b0}}), .in1(6'b010010), .out(multiplexer_26_out), .sel(and_109_out));
  Multiplexer #(.width(6), .enable("false")) multiplexer_27 (
    .in0({6{1'b0}}), .in1(6'b010011), .out(multiplexer_27_out), .sel(and_118_out));
  and and_118 (and_118_out, and_111_out, not_60_out);
  Multiplexer #(.width(6), .enable("false")) multiplexer_28 (
    .in0({6{1'b0}}), .in1(6'b010100), .out(multiplexer_28_out), .sel(and_119_out));
  and and_119 (and_119_out, and_113_out, func7[5]);
  Multiplexer #(.width(6), .enable("false")) multiplexer_29 (
    .in0({6{1'b0}}), .in1(6'b010101), .out(multiplexer_29_out), .sel(and_115_out));
  Multiplexer #(.width(6), .enable("false")) multiplexer_30 (
    .in0({6{1'b0}}), .in1(6'b010110), .out(multiplexer_30_out), .sel(and_117_out));
  assign I03_type_address = or_22_out | multiplexer_22_out;  // OR_Gate or_23, 6 bits wide
  assign or_24_out = multiplexer_23_out | multiplexer_24_out;  // OR_Gate or_24, 6 bits wide
  assign or_25_out = multiplexer_25_out | multiplexer_26_out;  // OR_Gate or_25, 6 bits wide
  assign or_26_out = multiplexer_27_out | multiplexer_28_out;  // OR_Gate or_26, 6 bits wide
  assign or_27_out = multiplexer_29_out | multiplexer_30_out;  // OR_Gate or_27, 6 bits wide
  assign or_28_out = or_24_out | or_25_out;  // OR_Gate or_28, 6 bits wide
  assign or_29_out = or_26_out | or_27_out;  // OR_Gate or_29, 6 bits wide
  assign I13_type_address = or_28_out | or_29_out;  // OR_Gate or_30, 6 bits wide
  not not_63 (not_63_out, func3[0]);
  not not_64 (not_64_out, func3[1]);
  not not_65 (not_65_out, func3[2]);
  not not_66 (not_66_out, func3[1]);
  not not_67 (not_67_out, func3[2]);
  not not_68 (not_68_out, func3[0]);
  not not_69 (not_69_out, func3[1]);
  not not_70 (not_70_out, func3[1]);
  not not_71 (not_71_out, func3[0]);
  and and_120 (and_120_out, SB_type[0], not_63_out);
  and and_121 (and_121_out, and_120_out, and_122_out);
  and and_122 (and_122_out, not_64_out, not_65_out);
  and and_123 (and_123_out, SB_type[0], func3[0]);
  and and_124 (and_124_out, and_123_out, and_125_out);
  and and_125 (and_125_out, not_66_out, not_67_out);
  and and_126 (and_126_out, SB_type[0], not_68_out);
  and and_127 (and_127_out, and_126_out, and_128_out);
  and and_128 (and_128_out, not_69_out, func3[2]);
  and and_129 (and_129_out, SB_type[0], func3[0]);
  and and_130 (and_130_out, and_129_out, and_131_out);
  and and_131 (and_131_out, not_70_out, func3[2]);
  and and_132 (and_132_out, SB_type[0], not_71_out);
  and and_133 (and_133_out, and_132_out, and_134_out);
  and and_134 (and_134_out, func3[1], func3[2]);
  and and_135 (and_135_out, SB_type[0], func3[0]);
  and and_136 (and_136_out, and_135_out, and_137_out);
  and and_137 (and_137_out, func3[1], func3[2]);
  Multiplexer #(.width(6), .enable("false")) multiplexer_31 (
    .in0({6{1'b0}}), .in1(6'b011010), .out(multiplexer_31_out), .sel(and_121_out));
  Multiplexer #(.width(6), .enable("false")) multiplexer_32 (
    .in0({6{1'b0}}), .in1(6'b011011), .out(multiplexer_32_out), .sel(and_124_out));
  Multiplexer #(.width(6), .enable("false")) multiplexer_33 (
    .in0({6{1'b0}}), .in1(6'b011100), .out(multiplexer_33_out), .sel(and_127_out));
  Multiplexer #(.width(6), .enable("false")) multiplexer_34 (
    .in0({6{1'b0}}), .in1(6'b011101), .out(multiplexer_34_out), .sel(and_130_out));
  Multiplexer #(.width(6), .enable("false")) multiplexer_35 (
    .in0({6{1'b0}}), .in1(6'b011110), .out(multiplexer_35_out), .sel(and_133_out));
  Multiplexer #(.width(6), .enable("false")) multiplexer_36 (
    .in0({6{1'b0}}), .in1(6'b011111), .out(multiplexer_36_out), .sel(and_136_out));
  assign or_31_out = multiplexer_31_out | multiplexer_32_out;  // OR_Gate or_31, 6 bits wide
  assign or_32_out = multiplexer_33_out | multiplexer_34_out;  // OR_Gate or_32, 6 bits wide
  assign or_33_out = multiplexer_35_out | multiplexer_36_out;  // OR_Gate or_33, 6 bits wide
  assign SB_type_address = or_31_out | or_35_out;  // OR_Gate or_34, 6 bits wide
  assign or_35_out = or_32_out | or_33_out;  // OR_Gate or_35, 6 bits wide

  // Other names for the same wires on the sheet: I03_type[3:1] = func3; I13_type[5:1] = {func7[5], func7[0], func3};
  //   R_type[5:1] = {func7[5], func7[0], func3}; S_type[3:1] = func3; SB_type[3:1] = func3;
  //   func7_0And4[1:0] = {func7[5], func7[0]}

  // Notes on the sheet:
  //   INPUTS to your circuit
  //   OUTPUTS
endmodule
