// Logisim project cpu.circ as structural Verilog: 1 circuit, main circuit main
module main (
  input  [31:0] INSTRUCTION,
  input  CLOCK,
  output [31:0] PROGRAM_COUNTER,
  output [31:0] ra,
  output [31:0] sp,
  output [31:0] t0,
  output [31:0] t1,
  output [31:0] t2,
  output [31:0] s0,
  output [31:0] s1,
  output [31:0] a0
);

  wire Asel, BrEq, BrLt, BrUn, BSel, Bsel_t, Byte_half_Sel, MemRW, PCSel, RWE;
  wire [1:0] WBSel;
  wire [2:0] immSel;
  wire [3:0] ALUSel;
  wire [7:0] multiplexer_6_out;
  wire [15:0] multiplexer_8_out;
  wire [16:0] multiplexer_9_out;
  wire [24:0] multiplexer_7_out;
  wire [31:0] A, ALUresult, B, imme, INSTRUCTION_1, multiplexer_1_out, multiplexer_2_out, multiplexer_3_out,
       PC_4, PC_WR, PROGRAM_COUNTER1, ReadData, ReadData_byte_half, rs1, rs2, Write_back;

  control_logic control_logic_1 (
    .BSel(Bsel_t), .RegWEn(RWE), .ASel(Asel), .ImmSel(immSel), .BrUn(BrUn), .PCSel(PCSel), .BrLt(BrLt),
    .BrEq(BrEq), .inst({INSTRUCTION_1[31:13], Byte_half_Sel, INSTRUCTION_1[11:7], BSel, INSTRUCTION_1[5:0]}),
    .ALUSel(ALUSel), .MemRW(MemRW), .WBSel(WBSel));
  Adder #(.width(32)) adder_1 (.a(PROGRAM_COUNTER), .b(32'h4), .out(PC_4));  // open: cin, cout
  Multiplexer #(.width(32), .enable("false")) multiplexer_1 (
    .in0(PC_4), .in1(ALUresult), .out(multiplexer_1_out), .sel(PCSel));
  Multiplexer #(.width(32), .enable("false")) multiplexer_2 (
    .in0(INSTRUCTION), .in1(32'h13), .out(multiplexer_2_out), .sel(PCSel));
  Register #(.width(32)) PC (.D(multiplexer_1_out), .clk(CLOCK), .Q(PROGRAM_COUNTER));  // open: en, clr
  Register #(.width(32)) register_1 (.D(PROGRAM_COUNTER), .clk(CLOCK), .Q(PROGRAM_COUNTER1));  // open: en, clr
  imm_gen imm_gen_1 (
    .ImmSel(immSel),
    .inst({INSTRUCTION_1[31:13], Byte_half_Sel, INSTRUCTION_1[11:7], BSel, INSTRUCTION_1[5:0]}), .imm(imme));
  Register #(.width(32)) register_2 (
    .D(multiplexer_2_out), .clk(CLOCK),
    .Q({INSTRUCTION_1[31:13], Byte_half_Sel, INSTRUCTION_1[11:7], BSel, INSTRUCTION_1[5:0]}));  // open: en, clr
  regfile_main RegFile (
    .rs2(INSTRUCTION_1[24:20]), .rd(INSTRUCTION_1[11:7]), .Read_Data_1(rs1), .Read_Data_2(rs2), .ra(ra),
    .sp(sp), .t0(t0), .t1(t1), .t2(t2), .s0(s0), .s1(s1), .a0(a0), .rs1(INSTRUCTION_1[19:15]),
    .Write_Data(Write_back), .RegWEn(RWE), .clk(CLOCK));
  Multiplexer #(.width(32), .enable("false")) multiplexer_3 (
    .in0(imme), .in1(rs1), .out(multiplexer_3_out), .sel(BSel));
  alu Arithmetic_Logic_Unit (.Result(ALUresult), .ALUSel(ALUSel), .A(A), .B(B));
  branch_comp branch_comp_1 (.BrEq(BrEq), .BrUn(BrUn), .rs1(multiplexer_3_out), .BrLt(BrLt), .rs2(rs2));
  Multiplexer #(.width(32), .enable("false")) multiplexer_4 (.in0(rs1), .in1(PROGRAM_COUNTER1), .out(A), .sel(Asel));
  Multiplexer #(.width(32), .enable("false")) multiplexer_5 (.in0(rs2), .in1(imme), .out(B), .sel(Bsel_t));
  Multiplexer #(.select(2), .width(8), .enable("false")) multiplexer_6 (
    .in0(ReadData[7:0]), .in1(ReadData[15:8]), .in2(ReadData[23:16]), .in3(ReadData[31:24]),
    .out(multiplexer_6_out), .sel(ALUresult[1:0]));
  // mem_main DMEM: pin names not known; wires that end beside it: ALUresult, rs2, CLOCK, MemRW, ReadData
  Multiplexer #(.width(25), .enable("false")) multiplexer_7 (
    .in0({25{1'b0}}), .in1({25{1'b1}}), .out(multiplexer_7_out), .sel(multiplexer_6_out[7]));
  Multiplexer #(.select(2), .width(16), .enable("false")) multiplexer_8 (
    .in0(ReadData[15:0]), .in1(ReadData[23:8]), .in2(ReadData[31:16]), .out(multiplexer_8_out),
    .sel(ALUresult[1:0]));  // open: in3
  Multiplexer #(.width(17), .enable("false")) multiplexer_9 (
    .in0({17{1'b0}}), .in1({17{1'b1}}), .out(multiplexer_9_out), .sel(multiplexer_8_out[15]));
  Register #(.width(32)) register_3 (.D(PC_4), .clk(CLOCK), .Q(PC_WR));  // open: en, clr
  Multiplexer #(.width(32), .enable("false")) multiplexer_10 (
    .in0({multiplexer_7_out, multiplexer_6_out[6:0]}), .in1({multiplexer_9_out, multiplexer_8_out[14:0]}),
    .out(ReadData_byte_half), .sel(Byte_half_Sel));
  Multiplexer #(.select(2), .width(32), .enable("false")) multiplexer_11 (
    .in0(PC_WR), .in1(ALUresult), .in2(ReadData), .in3(ReadData_byte_half), .out(Write_back), .sel(WBSel));

  // Other names for the same wires on the sheet: clk = CLOCK; INSTRUCTION_1 (some bits) = {Byte_half_Sel, BSel};
  //   rd_ad[4:0] = INSTRUCTION_1[11:7]; rs1_ad[4:0] = INSTRUCTION_1[19:15]; rs2_ad[4:0] = INSTRUCTION_1[24:20]

  // Notes on the sheet:
  //   Output
  //   IMEM (do **NOT** move this)
  //   Inputs
  //   It is OK to move the PC, RegFile, ALU, MEM, Branch Comp, Imm Gen, and Control Logic to wherever is most convenient for you when constructing your CPU, and to delete this text
  //   Inputs/Outputs for testing. Do **NOT** move these.
endmodule
