// Logisim project imm_gen.circ as structural Verilog: 1 circuit, main circuit imm_gen
module imm_gen (
  input  [31:0] inst,
  input  [2:0] ImmSel,
  output [31:0] imm
);

  wire [31:11] i_format, s_format;
  wire [31:12] b_format;
  wire [31:20] j_format;

  Multiplexer #(.width(20), .enable("false")) multiplexer_1 (
    .in0({20{1'b0}}), .in1({20{1'b1}}), .out(b_format), .sel(inst[31]));
  Multiplexer #(.width(21), .enable("false")) multiplexer_2 (
    .in0({21{1'b0}}), .in1({21{1'b1}}), .out(i_format), .sel(inst[31]));
  Multiplexer #(.width(21), .enable("false")) multiplexer_3 (
    .in0({21{1'b0}}), .in1({21{1'b1}}), .out(s_format), .sel(inst[31]));
  Multiplexer #(.width(12), .enable("false")) multiplexer_4 (
    .in0({12{1'b0}}), .in1({12{1'b1}}), .out(j_format), .sel(inst[31]));
  Multiplexer #(.select(3), .width(32), .enable("false")) multiplexer_5 (
    .in0({i_format, inst[30:20]}), .in1({s_format, inst[30:25], inst[11:7]}),
    .in2({b_format, inst[7], inst[30:25], inst[11:8], 1'b0}), .in3({inst[31:12], {12{1'b0}}}),
    .in4({j_format, inst[19:12], inst[20], inst[30:21], 1'b0}), .out(imm), .sel(ImmSel));  // open: in5, in6, in7

  // Other names for the same wires on the sheet: i_format[10:0] = inst[30:20];
  //   j_format[19:1] = {inst[19:12], inst[20], inst[30:21]}; u_format[31:12] = inst[31:12];
  //   b_format[11:1] = {inst[7], inst[30:25], inst[11:8]}; s_format[10:0] = {inst[30:25], inst[11:7]}

  // Notes on the sheet:
  //   INPUTS to your circuit
  //   DON'T CHANGE THE LOCATIONS OF THE INPUTS AND OUTPUTS!
  //   OUTPUT from your circuit
endmodule
